// Logisim project logisim.circ as structural Verilog
module ALU (
  input  [7:0] Accumulator,
  input  [7:0] BUS,
  input  Active,
  input  [2:0] Control_Unit,
  output [7:0] Accumulator_2
);

  wire [7:0] Inverter_output, multiplexer_1_out;

  Inverter Inverter (.Input(Accumulator), .Output(Inverter_output));
  Multiplexer #(.select(3), .width(8), .enable("false")) multiplexer_1 (
    .in0(Inverter_output), .out(multiplexer_1_out), .sel(Control_Unit));  // open: in1, in2, in3, in4, in5, in6, in7
  assign Accumulator_2 = Active ? multiplexer_1_out : 8'bz;  // Controlled_Buffer controlled_buffer_1
endmodule

module Inverter (
  input  [7:0] Input,
  output [7:0] Output
);

  not not_1 (Output[0], Input[0]);
  not not_2 (Output[1], Input[1]);
  not not_3 (Output[2], Input[2]);
  not not_4 (Output[3], Input[3]);
  not not_5 (Output[4], Input[4]);
  not not_6 (Output[5], Input[5]);
  not not_7 (Output[6], Input[6]);
  not not_8 (Output[7], Input[7]);
endmodule
